# Fritzing sketch Fogponics (saved by Fritzing 0.9.3b)
breadboards: 1

parts:
  Raspberry_Pi_1 = Raspberry Pi 3 [part_number=RPI-3-V1.2]
  U2 = SHT1x Humdity Sensor [package=sht1x]
  SW1 = PowerSwitch Tail II
  R1 = Resistor [tolerance=±5% resistance=10k package="0805 [SMD]"]

nets:
  3V3: Raspberry_Pi_1.3v3, Raspberry_Pi_1.3V3, U2.VDD, R1.Pin_0
  N1: Raspberry_Pi_1.GPIO2, U2.DATA, R1.Pin_1
  N2: Raspberry_Pi_1.GPIO3, U2.SCK
  GND: Raspberry_Pi_1.GND, U2.GND, SW1.-in
  N3: Raspberry_Pi_1.GPIO18, SW1.+in
